# Fritzing sketch arduino-sbus (saved by Fritzing 0.9.2b)
breadboards: 1

parts:
  Part1 = Arduino Uno (Rev3)
  Q1 = NPN-Transistor [part_number=PN2222A package="TO92 [THT]"]
  R1 = Resistor [tolerance=±5% resistance=10k package=THT]
  R2 = Resistor [tolerance=±5% resistance=1k package=THT]
  LED1 = LED - 5mm [color="Red (633nm)" package="5 mm [THT]"]
  R3 = Resistor [tolerance=±5% resistance=220 package=THT]
  LED2 = LED - 5mm [color="Red (633nm)" package="5 mm [THT]"]
  R4 = Resistor [tolerance=±5% resistance=220 package=THT]
  LED3 = LED - 5mm [color="Red (633nm)" package="5 mm [THT]"]
  R5 = Resistor [tolerance=±5% resistance=220 package=THT]
  LED4 = LED - 5mm [color="Red (633nm)" package="5 mm [THT]"]
  R6 = Resistor [tolerance=±5% resistance=220 package=THT]
  U1 = mystery part, 3 pins [chip_label=X8R]

nets:
  N1: Part1.D9_PWM, LED3.anode
  N2: Part1.D10_PWM/SS, LED4.anode
  N3: Part1.D0/RX, Q1.C, R2.Pin_0
  N4: Part1.D5_PWM, LED1.anode
  N5: Part1.D6_PWM, LED2.anode
  N6: Part1.5V, R2.Pin_1, U1.pin2
  N7: Part1.GND, Q1.E, R3.Pin_1, R4.Pin_1, R5.Pin_1, R6.Pin_1, U1.pin3
  N8: Q1.B, R1.Pin_1
  N9: R1.Pin_0, U1.pin1
  N10: LED1.cathode, R3.Pin_0
  N11: LED2.cathode, R4.Pin_0
  N12: LED3.cathode, R5.Pin_0
  N13: LED4.cathode, R6.Pin_0
