# Fritzing sketch teensy-sbus (saved by Fritzing 0.9.3b)
breadboards: 1

parts:
  Q1 = NPN-Transistor [part_number=PN2222A package="TO92 [THT]"]
  R1 = Resistor [tolerance=±5% resistance=10k package=THT]
  R2 = Resistor [tolerance=±5% resistance=1k package=THT]
  U1 = mystery part, 3 pins [chip_label=X8R]
  Teensy_3_1 = Teensy 3.2

nets:
  N1: Q1.E, U1.pin3, Teensy_3_1.GND
  N2: Q1.B, R1.Pin_1
  N3: Q1.C, R2.Pin_0, Teensy_3_1.D9
  N4: R1.Pin_0, U1.pin1
  N5: R2.Pin_1, U1.pin2, Teensy_3_1.Vin

custom parts:
  Teensy 3.2: The Teensy is a complete USB-based microcontoller development system, in a very small footprint, capable of implementing many types of projects. All programming is done via the USB port. No special programmer is needed, only a standard micro-USB cable and a PC or Macintosh with a USB port. It has a USB keyboard/mouse/joystick emulation stack and can be programmed through Arduino IDE.
